// Logisim project project2.circ as structural Verilog: 3 circuits, main circuit main
module main (
  input  C2,
  input  C1,
  input  C0,
  input  B3,
  input  B2,
  input  B1,
  input  B0,
  input  A3,
  input  A2,
  input  A1,
  input  A0,
  output V,
  output F3,
  output Z,
  output F2,
  output C,
  output F1,
  output S,
  output F0
);

  wire n7404_1_p3, n7404_1_p4, n7404_1_p6, n7404_1_p9, n7404_1_p10, n7404_1_p11, n7404_1_p12, n7408_1_p3,
       n7408_1_p8, n7408_1_p9, n7483_1__6__s2, n7483_1__14_cout, n7486_1_p3, n7486_1_p6, n7486_1_p11,
       n7486_1_p14, n7486_2_p3, n7486_2_p4, n7486_2_p5, n7486_2_p6, n74153_1_p7, n74153_1_p14, n74153_2_p7,
       n74153_2_p14;

  // _7486 7486_1: pin names not known; wires that end beside it: C0, B3, n7486_1_p3, C0, B2, n7486_1_p6, 1'b0, 1'b1, C0, B1, n7486_1_p11, C0, B0, n7486_1_p14
  // _74153 74153_1: pin names not known; wires that end beside it: 1'b0, C2, 1'b1, B3, 1'b0, n7486_1_p3, n74153_1_p7, 1'b0, C1, 1'b1, B2, 1'b0, n7486_1_p6, n74153_1_p14
  _7483 u_7483_1 (
    ._1__A4(n74153_2_p7), ._3__A3(n7483_1__6__s2), ._4__B3(n7408_1_p8), ._5__Vcc(1'b1),
    ._6__S2(n7483_1__6__s2), ._7__B2(1'b0), ._8__A2(1'b0), ._16__B4(A1), ._15__S4(F1),
    ._14_Cout(n7483_1__14_cout), ._13__Cin(n7404_1_p4), ._12__GND(1'b0), ._11__B1(A0),
    ._10__A1(n74153_2_p14), ._9__S1(F0));  // open: _2__S3
  // _74153 74153_2: pin names not known; wires that end beside it: 1'b0, C2, 1'b1, B1, 1'b0, n7486_1_p11, n74153_2_p7, 1'b0, C1, 1'b1, B0, 1'b0, n7486_1_p14, n74153_2_p14
  // _7486 7486_2: pin names not known; wires that end beside it: C1, C0, n7486_2_p3, n7486_2_p4, n7486_2_p5, n7486_2_p6, 1'b0, 1'b1
  _7483 u_7483_2 (
    ._1__A4(n74153_1_p7), ._3__A3(n7486_2_p4), ._4__B3(n7408_1_p8), ._5__Vcc(1'b1), ._6__S2(n7486_2_p4),
    ._7__B2(1'b0), ._8__A2(1'b0), ._16__B4(A3), ._15__S4(F3), ._14_Cout(n7486_2_p5), ._13__Cin(n7408_1_p9),
    ._12__GND(1'b0), ._11__B1(A2), ._10__A1(n74153_1_p14), ._9__S1(F2));  // open: _2__S3
  // _7408 7408_1: pin names not known; wires that end beside it: C2, n7486_2_p3, n7408_1_p3, C2, C0, 1'b1, n7483_1__14_cout, n7408_1_p8, n7408_1_p9, n7486_2_p5, n7408_1_p8, C
  // _7404 7404_1: pin names not known; wires that end beside it: n7408_1_p3, n7408_1_p8, n7404_1_p3, n7404_1_p4, 1'b0, n7404_1_p6, 1'b0, 1'b1, n7404_1_p9, n7404_1_p10, n7404_1_p11, n7404_1_p12
  // _7432 7432_1: pin names not known; wires that end beside it: n7404_1_p6, C1, n7404_1_p3, 1'b0, 1'b1, F0, F1, n7404_1_p9, F3, F2, n7404_1_p11
  // _7408 7408_2: pin names not known; wires that end beside it: n7486_2_p6, n7408_1_p8, V, 1'b0, 1'b1, n7404_1_p10, n7404_1_p12, Z

  assign S = F3;

  // Notes on the sheet:
  //   Y3
  //   Y2
  //   Y1
  //   Y0
  //   F1
  //   F0
  //   (c2(c1xorc0)
  //   (c1+C2C0)'
  //   F3
  //   F2
endmodule

module _7483 (
  input  _1__A4,
  input  _16__B4,
  input  _3__A3,
  input  _4__B3,
  input  _13__Cin,
  input  _5__Vcc,
  input  _12__GND,
  input  _11__B1,
  input  _7__B2,
  input  _10__A1,
  input  _8__A2,
  output _2__S3,
  output _15__S4,
  output _14_Cout,
  output _6__S2,
  output _9__S1
);

  wire and_1_out, and_2_out, and_3_out, and_4_out, and_5_out, and_6_out, and_7_out, and_8_out, and_9_out,
       and_10_out, and_11_out, and_12_out, and_13_out, and_14_out, nand_1_out, nand_2_out, nand_3_out,
       nand_4_out, nor_1_out, nor_2_out, nor_3_out, nor_4_out, nor_6_out, nor_7_out, nor_8_out, not_1_out,
       not_2_out, not_3_out, not_4_out, not_5_out, not_6_out;

  nand nand_1 (nand_1_out, _16__B4, _1__A4);
  nor nor_1 (nor_1_out, _16__B4, _1__A4);
  nand nand_2 (nand_2_out, _4__B3, _3__A3);
  nor nor_2 (nor_2_out, _4__B3, _3__A3);
  nand nand_3 (nand_3_out, _7__B2, _8__A2);
  nor nor_3 (nor_3_out, _7__B2, _8__A2);
  nand nand_4 (nand_4_out, _11__B1, _10__A1);
  nor nor_4 (nor_4_out, _11__B1, _10__A1);
  and and_1 (and_1_out, nor_2_out, nand_1_out);
  and and_2 (and_2_out, nor_3_out, nand_1_out, nand_2_out);
  and and_3 (and_3_out, nor_4_out, nand_1_out, nand_2_out, nand_3_out);
  and and_4 (and_4_out, nand_1_out, nand_2_out, nand_3_out, nand_4_out, not_2_out);
  not not_1 (not_1_out, nor_1_out);
  and and_5 (and_5_out, nor_3_out, nand_2_out);
  and and_6 (and_6_out, nor_4_out, nand_2_out, nand_3_out);
  and and_7 (and_7_out, nand_2_out, nand_3_out, nand_4_out, not_2_out);
  not not_2 (not_2_out, _13__Cin);
  not not_3 (not_3_out, nor_2_out);
  and and_8 (and_8_out, nor_4_out, nand_3_out);
  and and_9 (and_9_out, nand_3_out, nand_4_out, not_2_out);
  not not_4 (not_4_out, nor_3_out);
  and and_10 (and_10_out, nand_4_out, not_2_out);
  not not_5 (not_5_out, nor_4_out);
  not not_6 (not_6_out, not_2_out);
  nor nor_5 (_14_Cout, nor_1_out, and_1_out, and_2_out, and_3_out, and_4_out);
  and and_11 (and_11_out, nand_1_out, not_1_out);
  and and_12 (and_12_out, nand_2_out, not_3_out);
  and and_13 (and_13_out, nand_3_out, not_4_out);
  and and_14 (and_14_out, nand_4_out, not_5_out);
  xor xor_1 (_15__S4, and_11_out, nor_6_out);
  nor nor_6 (nor_6_out, nor_2_out, and_5_out, and_6_out, and_7_out);
  xor xor_2 (_2__S3, and_12_out, nor_7_out);
  nor nor_7 (nor_7_out, nor_3_out, and_8_out, and_9_out);
  xor xor_3 (_6__S2, and_13_out, nor_8_out);
  nor nor_8 (nor_8_out, nor_4_out, and_10_out);
  xor xor_4 (_9__S1, and_14_out, not_6_out);

  // Notes on the sheet:
  //   7483: 4-bit full adder
endmodule

module test (
  input  _1__A4,
  input  _16__B4,
  input  _3__A3,
  input  _4__B3,
  input  _13__Cin,
  input  _5__Vcc,
  input  _12__GND,
  input  _11__B1,
  input  _7__B2,
  input  _10__A1,
  input  _8__A2,
  output _2__S3,
  output _15__S4,
  output out_14,
  output _6__S2,
  output _9__S1
);

  wire and_1_out, and_2_out, and_3_out, and_4_out, and_5_out, and_6_out, and_7_out, and_8_out, and_9_out,
       and_10_out, and_11_out, and_12_out, and_13_out, and_14_out, nand_1_out, nand_2_out, nand_3_out,
       nand_4_out, nor_1_out, nor_2_out, nor_3_out, nor_4_out, nor_6_out, nor_7_out, nor_8_out, not_1_out,
       not_2_out, not_3_out, not_4_out, not_5_out, not_6_out;

  nand nand_1 (nand_1_out, _16__B4, _1__A4);
  nor nor_1 (nor_1_out, _16__B4, _1__A4);
  nand nand_2 (nand_2_out, _4__B3, _3__A3);
  nor nor_2 (nor_2_out, _4__B3, _3__A3);
  nand nand_3 (nand_3_out, _7__B2, _8__A2);
  nor nor_3 (nor_3_out, _7__B2, _8__A2);
  nand nand_4 (nand_4_out, _11__B1, _10__A1);
  nor nor_4 (nor_4_out, _11__B1, _10__A1);
  and and_1 (and_1_out, nor_2_out, nand_1_out);
  and and_2 (and_2_out, nor_3_out, nand_1_out, nand_2_out);
  and and_3 (and_3_out, nor_4_out, nand_1_out, nand_2_out, nand_3_out);
  and and_4 (and_4_out, nand_1_out, nand_2_out, nand_3_out, nand_4_out, not_2_out);
  not not_1 (not_1_out, nor_1_out);
  and and_5 (and_5_out, nor_3_out, nand_2_out);
  and and_6 (and_6_out, nor_4_out, nand_2_out, nand_3_out);
  and and_7 (and_7_out, nand_2_out, nand_3_out, nand_4_out, not_2_out);
  not not_2 (not_2_out, _13__Cin);
  not not_3 (not_3_out, nor_2_out);
  and and_8 (and_8_out, nor_4_out, nand_3_out);
  and and_9 (and_9_out, nand_3_out, nand_4_out, not_2_out);
  not not_4 (not_4_out, nor_3_out);
  and and_10 (and_10_out, nand_4_out, not_2_out);
  not not_5 (not_5_out, nor_4_out);
  not not_6 (not_6_out, not_2_out);
  nor nor_5 (out_14, nor_1_out, and_1_out, and_2_out, and_3_out, and_4_out);
  and and_11 (and_11_out, nand_1_out, not_1_out);
  and and_12 (and_12_out, nand_2_out, not_3_out);
  and and_13 (and_13_out, nand_3_out, not_4_out);
  and and_14 (and_14_out, nand_4_out, not_5_out);
  xor xor_1 (_15__S4, and_11_out, nor_6_out);
  nor nor_6 (nor_6_out, nor_2_out, and_5_out, and_6_out, and_7_out);
  xor xor_2 (_2__S3, and_12_out, nor_7_out);
  nor nor_7 (nor_7_out, nor_3_out, and_8_out, and_9_out);
  xor xor_3 (_6__S2, and_13_out, nor_8_out);
  nor nor_8 (nor_8_out, nor_4_out, and_10_out);
  xor xor_4 (_9__S1, and_14_out, not_6_out);

  // Notes on the sheet:
  //   7483: 4-bit full adder
endmodule
