// Logisim project Controll_Unit.circ as structural Verilog: 1 circuit, main circuit main
module main (
  input  [3:0] in_1,
  output [2:0] ALUOp,
  output ALUSrc,
  output Bneq,
  output Beq,
  output MemToReg,
  output MemWrite,
  output MemRead,
  output RegWrite,
  output RegDst,
  output Shift,
  output Jump
);

  ROM #(.addrWidth(4), .dataWidth(13)) rom_1 (
    .addr(in_1), .data({Jump, Shift, RegDst, RegWrite, MemRead, MemWrite, MemToReg, Beq, Bneq, ALUSrc, ALUOp}));  // open: sel

  // Notes on the sheet:
  //   contents of rom_1 (hex, n*v repeats v):
  //   603 208 601 209 1000 11 88 348 602 e0e e0d 20b 604 20a 21 600
endmodule
