// Logisim project EX_MEM.circ as structural Verilog: 1 circuit, main circuit main
module main (
  input  CLR,
  input  clk,
  input  [7:0] alu_result,
  input  [3:0] reg_rd_addrs,
  input  regwrt,
  input  MemtoReg,
  input  Memread,
  input  Memwrite,
  input  beq,
  input  bneq,
  output [7:0] alu_reslt,
  output [3:0] reg_rd_addrs_2,
  output reg_wrt,
  output MemtoReg_2,
  output Memread_2,
  output memwrite_2,
  output beq_2,
  output bneq_2
);

  Register u_alu_result (.D(alu_result), .en(1'b1), .Q(alu_reslt), .clk(clk), .clr(CLR));
  Register #(.width(4)) reg_rd (.D(reg_rd_addrs), .en(1'b1), .Q(reg_rd_addrs_2), .clk(clk), .clr(CLR));
  Register #(.width(1)) register_1 (.D(regwrt), .en(1'b1), .Q(reg_wrt), .clk(clk), .clr(CLR));
  Register #(.width(1)) register_2 (.D(MemtoReg), .en(1'b1), .Q(MemtoReg_2), .clk(clk), .clr(CLR));
  Register #(.width(1)) register_3 (.D(Memread), .en(1'b1), .Q(Memread_2), .clk(clk), .clr(CLR));
  Register #(.width(1)) register_4 (.D(Memwrite), .en(1'b1), .Q(memwrite_2), .clk(clk), .clr(CLR));
  Register #(.width(1)) register_5 (.D(beq), .en(1'b1), .Q(beq_2), .clk(clk), .clr(CLR));
  Register #(.width(1)) register_6 (.D(bneq), .en(1'b1), .Q(bneq_2), .clk(clk), .clr(CLR));
endmodule
