// Logisim project Forward_Unit.circ as structural Verilog: 2 circuits, main circuit main
module main (
  input  EX_MEM_RegWrite,
  input  [3:0] EX_MEM_RegisterRD,
  input  [3:0] ID_EX_RegisterRs,
  input  [3:0] ID_EX_RegisterRt,
  input  [3:0] Mem_WB_RegisterRd,
  input  MEM_WB_RegWrite,
  output [1:0] ForwardA,
  output [1:0] ForwarB
);

  wire comparator_1_eq, comparator_2_eq, comparator_3_eq, comparator_4_eq, comparator_5_eq, comparator_6_eq;
  wire [3:0] and_4_out;

  Comparator #(.width(4), .mode("unsigned")) comparator_1 (
    .a(EX_MEM_RegisterRD), .b(4'b0000), .eq(comparator_1_eq));  // open: gt, lt
  Comparator #(.width(4), .mode("unsigned")) comparator_2 (
    .a(EX_MEM_RegisterRD), .b(ID_EX_RegisterRs), .eq(comparator_2_eq));  // open: gt, lt
  Comparator #(.width(4), .mode("unsigned")) comparator_3 (
    .a(Mem_WB_RegisterRd), .b(ID_EX_RegisterRs), .eq(comparator_3_eq));  // open: gt, lt
  Comparator #(.width(4), .mode("unsigned")) comparator_4 (
    .a(EX_MEM_RegisterRD), .b(ID_EX_RegisterRt), .eq(comparator_4_eq));  // open: gt, lt
  Comparator #(.width(4), .mode("unsigned")) comparator_5 (
    .a(Mem_WB_RegisterRd), .b(ID_EX_RegisterRt), .eq(comparator_5_eq));  // open: gt, lt
  Comparator #(.width(4), .mode("unsigned")) comparator_6 (
    .a(Mem_WB_RegisterRd), .b(4'b0000), .eq(comparator_6_eq));  // open: gt, lt
  and and_1 (and_4_out[3], ~comparator_1_eq, EX_MEM_RegWrite, comparator_2_eq);  // AND_Gate
  and and_2 (and_4_out[1], MEM_WB_RegWrite, ~comparator_6_eq, comparator_3_eq);  // AND_Gate
  and and_3 (and_4_out[2], EX_MEM_RegWrite, ~comparator_1_eq, comparator_4_eq);  // AND_Gate
  and and_4 (and_4_out[0], comparator_5_eq, ~comparator_6_eq, MEM_WB_RegWrite);  // AND_Gate
  ROM #(.addrWidth(4), .dataWidth(4)) rom_1 (.addr(and_4_out), .data({ForwardA, ForwarB}), .sel(1'b1));

  // Notes on the sheet:
  //   contents of rom_1 (hex, n*v repeats v):
  //   0 1 4 5 2 2 6 6 8 9 8 9 4*a
endmodule

module pseudo (
  input  [3:0] ID_EX_Reg_rt,
  input  [3:0] ID_EX_Reg_rs,
  input  [3:0] MEM_WB_Red_rd,
  input  [3:0] EX_MEM_Reg_rd,
  output [1:0] FORWARD_A,
  output [1:0] FORWARD_B
);

  wire nor_1_out, nor_2_out, nor_3_out, nor_4_out, or_1_out, or_2_out;
  wire [3:0] and_4_out, subtractor_1_out, subtractor_2_out, subtractor_3_out, subtractor_4_out;

  Subtractor #(.width(4)) subtractor_1 (
    .a(EX_MEM_Reg_rd), .b(ID_EX_Reg_rs), .out(subtractor_1_out));  // open: bin, bout
  Subtractor #(.width(4)) subtractor_2 (
    .a(EX_MEM_Reg_rd), .b(ID_EX_Reg_rt), .out(subtractor_2_out));  // open: bin, bout
  Subtractor #(.width(4)) subtractor_3 (
    .a(MEM_WB_Red_rd), .b(ID_EX_Reg_rs), .out(subtractor_3_out));  // open: bin, bout
  Subtractor #(.width(4)) subtractor_4 (
    .a(MEM_WB_Red_rd), .b(ID_EX_Reg_rt), .out(subtractor_4_out));  // open: bin, bout
  or or_1 (or_1_out, EX_MEM_Reg_rd[0], EX_MEM_Reg_rd[1], EX_MEM_Reg_rd[2], EX_MEM_Reg_rd[3]);
  nor nor_1 (nor_1_out, subtractor_2_out[0], subtractor_2_out[1], subtractor_2_out[2], subtractor_2_out[3]);
  nor nor_2 (nor_2_out, subtractor_1_out[0], subtractor_1_out[1], subtractor_1_out[2], subtractor_1_out[3]);
  nor nor_3 (nor_3_out, subtractor_3_out[0], subtractor_3_out[1], subtractor_3_out[2], subtractor_3_out[3]);
  nor nor_4 (nor_4_out, subtractor_4_out[0], subtractor_4_out[1], subtractor_4_out[2], subtractor_4_out[3]);
  and and_1 (and_4_out[3], or_1_out, nor_2_out);
  and and_2 (and_4_out[2], or_1_out, nor_1_out);
  or or_2 (or_2_out, MEM_WB_Red_rd[0], MEM_WB_Red_rd[1], MEM_WB_Red_rd[2], MEM_WB_Red_rd[3]);
  and and_3 (and_4_out[1], nor_3_out, or_2_out);
  and and_4 (and_4_out[0], nor_4_out, or_2_out);
  ROM #(.addrWidth(4), .dataWidth(4)) rom_1 (.addr(and_4_out), .data({FORWARD_A, FORWARD_B}), .sel(1'b1));

  // Notes on the sheet:
  //   contents of rom_1 (hex, n*v repeats v):
  //   0 1 4 5 2 2 6 6 8 9 8 9 4*a
endmodule
