// Logisim project ID_EX_reg.circ as structural Verilog: 1 circuit, main circuit main
module main (
  input  CLR,
  input  CLK,
  input  [7:0] pc_4,
  input  [7:0] reg_data_1,
  input  [7:0] reg_data_2,
  input  [7:0] IMM,
  input  [3:0] reg_rd_address,
  input  [3:0] reg_rs_address,
  input  [3:0] reg_rt_address,
  input  [2:0] Alu_op,
  input  reg_wrt,
  input  MemtoReg,
  input  Memread,
  input  Memwrite,
  input  regdst,
  input  shift,
  input  Jump,
  input  AluSRC,
  input  beq,
  input  bneq,
  output [7:0] reg_rs_data,
  output [7:0] reg_rt_data,
  output [3:0] reg_rd_address_2,
  output [3:0] reg_rs_address_2,
  output [3:0] reg_rt_address_2,
  output [2:0] Aluop,
  output reg_wrt_2,
  output MemtoReg_2,
  output Memread_2,
  output memwrite_2,
  output reg_dst,
  output shift_2,
  output jump_2,
  output Alusrc_2,
  output beq_2,
  output bneq_2
);

  Register read_reg1_data (.D(pc_4), .en(1'b1), .clk(CLK), .clr(CLR));  // open: Q
  Register read_reg1_data_2 (.D(reg_data_1), .en(1'b1), .Q(reg_rs_data), .clk(CLK), .clr(CLR));
  Register read_reg2_data (.D(reg_data_2), .en(1'b1), .Q(reg_rt_data), .clk(CLK), .clr(CLR));
  Register read_reg2_data_2 (.D(IMM), .en(1'b1), .clk(CLK), .clr(CLR));  // open: Q
  Register #(.width(4)) reg_rd (.D(reg_rd_address), .en(1'b1), .Q(reg_rd_address_2), .clk(CLK), .clr(CLR));
  Register #(.width(4)) reg_rs (.D(reg_rs_address), .en(1'b1), .Q(reg_rs_address_2), .clk(CLK), .clr(CLR));
  Register #(.width(4)) reg_rt (.D(reg_rt_address), .en(1'b1), .Q(reg_rt_address_2), .clk(CLK), .clr(CLR));
  Register #(.width(3)) register_1 (.D(Alu_op), .en(1'b1), .Q(Aluop), .clk(CLK), .clr(CLR));
  Register #(.width(1)) register_2 (.D(reg_wrt), .en(1'b1), .Q(reg_wrt_2), .clk(CLK), .clr(CLR));
  Register #(.width(1)) register_3 (.D(MemtoReg), .en(1'b1), .Q(MemtoReg_2), .clk(CLK));  // open: clr
  Register #(.width(1)) register_4 (.D(Memread), .en(1'b1), .Q(Memread_2), .clk(CLK), .clr(CLR));
  Register #(.width(1)) register_5 (.D(Memwrite), .en(1'b1), .Q(memwrite_2), .clk(CLK), .clr(CLR));
  Register #(.width(1)) register_6 (.D(regdst), .en(1'b1), .Q(reg_dst), .clk(CLK), .clr(CLR));
  Register #(.width(1)) register_7 (.D(shift), .en(1'b1), .Q(shift_2), .clk(CLK), .clr(CLR));
  Register #(.width(1)) register_8 (.D(Jump), .en(1'b1), .Q(jump_2), .clk(CLK), .clr(CLR));
  Register #(.width(1)) register_9 (.D(AluSRC), .en(1'b1), .Q(Alusrc_2), .clk(CLK), .clr(CLR));
  Register #(.width(1)) register_10 (.D(beq), .en(1'b1), .Q(beq_2), .clk(CLK), .clr(CLR));
  Register #(.width(1)) register_11 (.D(bneq), .en(1'b1), .Q(bneq_2), .clk(CLK), .clr(CLR));
endmodule
