// Logisim project IF_ID_reg.circ as structural Verilog: 1 circuit, main circuit main
module main (
  input  [7:0] Pc_4,
  input  [19:0] Instruction_0_19,
  input  Stall,
  input  CLK,
  input  CLR,
  output [7:0] PC_4_2,
  output [19:0] Instruction_0_19_2
);

  wire not_1_out;

  not not_1 (not_1_out, Stall);
  Register u_PC_4 (.D(Pc_4), .en(not_1_out), .Q(PC_4_2), .clk(CLK), .clr(CLR));
  Register #(.width(20)) IF_ID (.D(Instruction_0_19), .en(not_1_out), .Q(Instruction_0_19_2), .clk(CLK), .clr(CLR));
endmodule
