// Logisim project Instruction memory.circ as structural Verilog: 1 circuit, main circuit main
module main (
  input  [3:0] PC,
  output [19:0] Instructiion_0_19
);

  ROM #(.addrWidth(4), .dataWidth(20)) rom_1 (.addr(PC), .data(Instructiion_0_19));  // open: sel

  // Notes on the sheet:
  //   contents of rom_1 (hex, n*v repeats v):
  //   0 ed d 1212 0 1 0 1 101
endmodule
