// Logisim project MEM_WB.circ as structural Verilog: 1 circuit, main circuit main
module main (
  input  CLR,
  input  clk,
  input  [7:0] alu_result,
  input  [3:0] reg_rd_addrs,
  input  WB,
  output [7:0] alu_reslt,
  output [3:0] reg_rd_addrs_2,
  output reg_wrt
);

  Register u_alu_result (.D(alu_result), .en(1'b1), .Q(alu_reslt), .clk(clk), .clr(CLR));
  Register #(.width(4)) reg_rd (.D(reg_rd_addrs), .en(1'b1), .Q(reg_rd_addrs_2), .clk(clk), .clr(CLR));
  Register #(.width(1)) u_WB (.D(WB), .en(1'b1), .Q(reg_wrt), .clk(clk), .clr(CLR));
endmodule
