// Logisim project Main2.circ as structural Verilog: 2 circuits, main circuit main
module main (
  input  Clear,
  output [7:0] PC,
  output [7:0] jump_Data,
  output [3:0] Write_reg,
  output [7:0] Write_Data,
  output [7:0] Zero,
  output [7:0] t0,
  output [7:0] t1,
  output [7:0] t2,
  output [7:0] t3,
  output [7:0] t4,
  output [7:0] t5,
  output [7:0] sp
);

  wire alu_8_by_art_1_p4, Clk_out, main_1_alusrc, main_1_beq, main_1_bneq, main_1_jump, main_1_memread,
       main_1_memtoreg, main_1_memwrite, main_1_regdst, main_1_regwrite, main_1_shift;
  wire [2:0] main_1_aluop;
  wire [7:0] adder_1_out, alu_8_by_art_1_p5, multiplexer_3_out, multiplexer_4_out, multiplexer_5_out,
       ram_1_data, register_2_read_data_1, register_2_read_data_2, rom_1_data_2;
  wire [19:4] rom_1_data;

  Clock Clk (.out(Clk_out));
  Register register_1 (.D(jump_Data), .Q(PC), .clk(Clk_out), .clr(Clear));  // open: en
  Adder adder_1 (.a(PC), .b(8'h1), .out(adder_1_out), .cin(1'b0));  // open: cout
  ROM #(.dataWidth(20)) rom_1 (.addr(PC), .data({rom_1_data, rom_1_data_2[3:0]}));  // open: sel
  Multiplexer #(.width(4), .enable("false")) multiplexer_1 (
    .in0(rom_1_data[11:8]), .in1(rom_1_data[7:4]), .out(Write_reg), .sel(main_1_regdst));
  Multiplexer #(.width(4), .enable("false")) multiplexer_2 (
    .in0(rom_1_data[7:4]), .in1(4'b0000), .out(rom_1_data_2[7:4]), .sel(main_1_shift));
  Controll_Unit_main main_1 (
    .in_1(rom_1_data[19:16]), .ALUOp(main_1_aluop), .ALUSrc(main_1_alusrc), .Bneq(main_1_bneq),
    .Beq(main_1_beq), .MemToReg(main_1_memtoreg), .MemWrite(main_1_memwrite), .MemRead(main_1_memread),
    .RegWrite(main_1_regwrite), .RegDst(main_1_regdst), .Shift(main_1_shift), .Jump(main_1_jump));
  register register_2 (
    .Read_Register_1(rom_1_data[15:12]), .Read_Register_2(rom_1_data[11:8]), .Write_Register(Write_reg),
    .Write_Data(Write_Data), .Write_Signal(main_1_regwrite), .CLK(Clk_out), .Clear(Clear), .zero(Zero),
    .t0(t0), .t1(t1), .t2(t2), .t3(t3), .t4(t4), .t5(t5), .sp(sp), .Read_Data_1(register_2_read_data_1),
    .Read_Data_2(register_2_read_data_2));
  Multiplexer #(.width(8), .enable("false")) multiplexer_3 (
    .in0(register_2_read_data_2), .in1(rom_1_data_2), .out(multiplexer_3_out), .sel(main_1_alusrc));
  Multiplexer #(.select(3), .width(8), .enable("false")) multiplexer_4 (
    .in0(register_2_read_data_1), .in1(register_2_read_data_1), .in2(register_2_read_data_1),
    .in3(register_2_read_data_1), .in4(register_2_read_data_1), .in5(multiplexer_3_out),
    .in6(multiplexer_3_out), .in7(multiplexer_3_out), .out(multiplexer_4_out), .sel(main_1_aluop));
  Multiplexer #(.select(3), .width(8), .enable("false")) multiplexer_5 (
    .in0(multiplexer_3_out), .in1(multiplexer_3_out), .in2(multiplexer_3_out), .in3(multiplexer_3_out),
    .in4(multiplexer_3_out), .in5(register_2_read_data_1), .in6(register_2_read_data_1),
    .in7(register_2_read_data_1), .out(multiplexer_5_out), .sel(main_1_aluop));
  // ALU_8_by_ART alu_8_by_art_1: pin names not known; wires that end beside it: multiplexer_4_out, multiplexer_5_out, main_1_aluop, alu_8_by_art_1_p4, alu_8_by_art_1_p5
  addressHandler_main main_2 (
    .PC_4(adder_1_out), .Combined_end_of_splitter(rom_1_data[15:8]), .jumping_address(rom_1_data_2),
    .bneq(main_1_bneq), .ZeroOfAdder(alu_8_by_art_1_p4), .beq(main_1_beq), .JUMP(main_1_jump),
    .MUX_output(jump_Data));
  RAM #(.bus("separate")) ram_1 (
    .addr(alu_8_by_art_1_p5), .din(register_2_read_data_2), .data(ram_1_data), .str(main_1_memwrite),
    .clk(Clk_out), .ld(main_1_memread), .clr(Clear));  // open: sel
  Multiplexer #(.width(8), .enable("false")) multiplexer_6 (
    .in0(alu_8_by_art_1_p5), .in1(ram_1_data), .out(Write_Data), .sel(main_1_memtoreg));

  // Notes on the sheet:
  //   contents of rom_1 (hex, n*v repeats v):
  //   107ff 1010a 10201 e210b 10202 e2109 10201 10301 10502 f2340 f0320 f0430 15501 515fb 41000 10401
  //   67400 37701 94014 67100 37701 a1055 67500 37701 655a2 67500 37701 752a2 67200 37701 12388 67300
  //   37701 33481 24340 67400 37701 10146 10255 1230 67300 37701 b34fe 67400 37701 10480 105aa 84520 67200
  //   37701 d23ff 67300 37701 43500
  //   Alu_op
  //   Alu_src
  //   Bneq
  //   Beq
  //   MemToReg
  //   MemWrite
  //   MemRead
  //   RegWrite
  //   RegDst
  //   Shift
  //   Jump
endmodule

module register (
  input  [3:0] Read_Register_1,
  input  [3:0] Read_Register_2,
  input  [3:0] Write_Register,
  input  [7:0] Write_Data,
  input  Write_Signal,
  input  CLK,
  input  Clear,
  output [7:0] Read_Data_1,
  output [7:0] Read_Data_2,
  output [7:0] sp,
  output [7:0] zero,
  output [7:0] t5,
  output [7:0] t0,
  output [7:0] t4,
  output [7:0] t1,
  output [7:0] t2,
  output [7:0] t3
);

  wire and_1_out, and_2_out, and_3_out, and_4_out, and_5_out, and_6_out, and_7_out, and_8_out,
       decoder_1_out0, decoder_1_out1, decoder_1_out2, decoder_1_out3, decoder_1_out4, decoder_1_out5,
       decoder_1_out6, decoder_1_out7, multiplexer_1_out, multiplexer_3_out;
  wire [7:0] multiplexer_2_out;

  Decoder #(.select(4), .enable("false")) decoder_1 (
    .out0(decoder_1_out0), .out1(decoder_1_out1), .out2(decoder_1_out2), .out3(decoder_1_out3),
    .out4(decoder_1_out4), .out5(decoder_1_out5), .out6(decoder_1_out6), .out7(decoder_1_out7),
    .sel(Write_Register));  // open: out8, out9, out10, out11, out12, out13, out14, out15
  and and_1 (and_1_out, decoder_1_out0, 1'b0);
  and and_2 (and_2_out, decoder_1_out1, Write_Signal);
  and and_3 (and_3_out, decoder_1_out2, Write_Signal);
  and and_4 (and_4_out, decoder_1_out3, Write_Signal);
  and and_5 (and_5_out, decoder_1_out4, Write_Signal);
  and and_6 (and_6_out, decoder_1_out5, Write_Signal);
  and and_7 (and_7_out, decoder_1_out6, Write_Signal);
  and and_8 (and_8_out, decoder_1_out7, Write_Signal);
  Multiplexer #(.enable("false")) multiplexer_1 (.in0(and_8_out), .in1(Clear), .out(multiplexer_1_out), .sel(Clear));
  Multiplexer #(.width(8), .enable("false")) multiplexer_2 (
    .in0(Write_Data), .in1({8{1'b1}}), .out(multiplexer_2_out), .sel(Clear));
  Register u_zero (.D(Write_Data), .en(and_1_out), .Q(zero), .clk(CLK), .clr(Clear));
  Register u_t0 (.D(Write_Data), .en(and_2_out), .Q(t0), .clk(CLK), .clr(Clear));
  Register u_t1 (.D(Write_Data), .en(and_3_out), .Q(t1), .clk(CLK), .clr(Clear));
  Register u_t2 (.D(Write_Data), .en(and_4_out), .Q(t2), .clk(CLK), .clr(Clear));
  Register u_t3 (.D(Write_Data), .en(and_5_out), .Q(t3), .clk(CLK), .clr(Clear));
  Register u_t4 (.D(Write_Data), .en(and_6_out), .Q(t4), .clk(CLK), .clr(Clear));
  Register u_t5 (.D(Write_Data), .en(and_7_out), .Q(t5), .clk(CLK), .clr(Clear));
  Register u_sp (.D(multiplexer_2_out), .en(multiplexer_1_out), .Q(sp), .clk(multiplexer_3_out));  // open: clr
  Multiplexer #(.enable("false")) multiplexer_3 (.in0(CLK), .in1(Clear), .out(multiplexer_3_out), .sel(Clear));
  Multiplexer #(.select(4), .width(8), .enable("false")) multiplexer_4 (
    .in0(zero), .in1(t0), .in2(t1), .in3(t2), .in4(t3), .in5(t4), .in6(t5), .in7(sp), .out(Read_Data_1),
    .sel(Read_Register_1));  // open: in8, in9, in10, in11, in12, in13, in14, in15
  Multiplexer #(.select(4), .width(8), .enable("false")) multiplexer_5 (
    .in0(zero), .in1(t0), .in2(t1), .in3(t2), .in4(t3), .in5(t4), .in6(t5), .in7(sp), .out(Read_Data_2),
    .sel(Read_Register_2));  // open: in8, in9, in10, in11, in12, in13, in14, in15
endmodule
