// Logisim project Mem_Web.circ as structural Verilog: 1 circuit, main circuit main
module main (
  input  Reg_Write,
  input  Memto_Reg,
  input  [7:0] Read_data,
  input  [7:0] Alu_result,
  input  [3:0] Reg_rd_address,
  input  in_6,
  output Reg_write_2,
  output Memto_reg_2,
  output [7:0] Read_Data_2,
  output [7:0] Alu_Result_2,
  output [3:0] Reg_Rd_address_2
);

  wire clock_1_out;

  Clock clock_1 (.out(clock_1_out));
  Register #(.width(1)) register_1 (.D(Reg_Write), .en(1'b1), .Q(Reg_write_2), .clk(clock_1_out), .clr(in_6));
  Register #(.width(1)) register_2 (.D(Memto_Reg), .en(1'b1), .Q(Memto_reg_2), .clk(clock_1_out), .clr(in_6));
  Register u_alu_result (.D(Read_data), .en(1'b1), .Q(Read_Data_2), .clk(clock_1_out), .clr(in_6));
  Register u_alu_result_2 (.D(Alu_result), .en(1'b1), .Q(Alu_Result_2), .clk(clock_1_out), .clr(in_6));
  Register #(.width(4)) reg_rd (.D(Reg_rd_address), .en(1'b1), .Q(Reg_Rd_address_2), .clk(clock_1_out), .clr(in_6));
endmodule
