// Logisim project Processor1.circ as structural Verilog
module registers (
  input  [3:0] Input_for_reg_1,
  input  [3:0] Input_for_reg_2,
  input  [3:0] input_for_write_reg,
  input  [7:0] Write_register_data,
  input  reg_write,
  input  Clock_pulse,
  input  Clear,
  output [7:0] output_reg_1,
  output [7:0] output_reg_2,
  output [7:0] Zero,
  output [7:0] t0,
  output [7:0] t1,
  output [7:0] t2,
  output [7:0] t3,
  output [7:0] t4,
  output [7:0] T5,
  output [7:0] sp
);

  wire and_1_out, decoder_1_out0, decoder_1_out1, decoder_1_out2, decoder_1_out3, decoder_1_out4,
       decoder_1_out5, decoder_1_out6, decoder_1_out7;
  wire [2:0] multiplexer_1_out;

  and and_1 (and_1_out, Clock_pulse, reg_write);
  Multiplexer #(.width(3), .enable("false")) multiplexer_1 (
    .in0(3'b000), .in1(input_for_write_reg[2:0]), .out(multiplexer_1_out), .sel(and_1_out));
  Decoder #(.select(3), .enable("false")) decoder_1 (
    .out0(decoder_1_out0), .out1(decoder_1_out1), .out2(decoder_1_out2), .out3(decoder_1_out3),
    .out4(decoder_1_out4), .out5(decoder_1_out5), .out6(decoder_1_out6), .out7(decoder_1_out7),
    .sel(multiplexer_1_out));
  Register zero_reg (.D({8{1'b0}}), .en(1'b1), .Q(Zero), .clk(decoder_1_out0), .clr(Clear));
  Register t0_reg (.D(Write_register_data), .en(1'b1), .Q(t0), .clk(decoder_1_out1), .clr(Clear));
  Register t1_reg (.D(Write_register_data), .en(1'b1), .Q(t1), .clk(decoder_1_out2), .clr(Clear));
  Register t2_reg (.D(Write_register_data), .en(1'b1), .Q(t2), .clk(decoder_1_out3), .clr(Clear));
  Register t3_reg (.D(Write_register_data), .en(1'b1), .Q(t3), .clk(decoder_1_out4), .clr(Clear));
  Register t4_reg (.D(Write_register_data), .en(1'b1), .Q(t4), .clk(decoder_1_out5), .clr(Clear));
  Register sp_reg (.D(Write_register_data), .en(1'b1), .Q(sp), .clk(decoder_1_out6), .clr(Clear));
  Register t5_reg (.D(Write_register_data), .en(1'b1), .Q(T5), .clk(decoder_1_out7), .clr(Clear));
  Multiplexer #(.select(3), .width(8), .enable("false")) multiplexer_2 (
    .in0(Zero), .in1(t0), .in2(t1), .in3(t2), .in4(t3), .in5(t4), .in6(sp), .in7(T5), .out(output_reg_2),
    .sel(Input_for_reg_2[2:0]));
  Multiplexer #(.select(3), .width(8), .enable("false")) multiplexer_3 (
    .in0(Zero), .in1(t0), .in2(t1), .in3(t2), .in4(t3), .in5(t4), .in6(sp), .in7(T5), .out(output_reg_1),
    .sel(Input_for_reg_1[2:0]));
endmodule

module data_memory (
  input  Memory_Write,
  input  Memory_Read,
  input  [7:0] output_for_ALU,
  input  Memory_to_register_selection,
  input  [7:0] reg2_output,
  input  Clock_Pulse,
  output [7:0] write_register_data,
  output [7:0] out_8
);

  RAM #(.bus("separate")) ram_1 (
    .addr(output_for_ALU), .din(reg2_output), .data(out_8), .str(Memory_Write), .clk(Clock_Pulse),
    .ld(Memory_Read));  // open: sel, clr
  Multiplexer #(.width(8), .enable("false")) multiplexer_1 (
    .in0(output_for_ALU), .in1(out_8), .out(write_register_data), .sel(Memory_to_register_selection));
endmodule
