// Logisim project addressHandler.circ as structural Verilog: 1 circuit, main circuit main
module main (
  input  [7:0] PC_4,
  input  [7:0] Combined_end_of_splitter,
  input  [7:0] jumping_address,
  input  bneq,
  input  ZeroOfAdder,
  input  beq,
  input  JUMP,
  output [7:0] MUX_output
);

  wire and_1_out, and_2_out, not_1_out;
  wire [1:0] priority_encoder_1_out;
  wire [7:0] adder_1_out;

  not not_1 (not_1_out, ZeroOfAdder);
  and and_1 (and_1_out, bneq, not_1_out);
  and and_2 (and_2_out, beq, ZeroOfAdder);
  Adder adder_1 (.a(PC_4), .b(jumping_address), .out(adder_1_out));  // open: cin, cout
  Priority_Encoder #(.select(2)) priority_encoder_1 (
    .in0(1'b1), .in1(and_1_out), .in2(and_2_out), .in3(JUMP), .out(priority_encoder_1_out));  // open: gs, en_out, en_in
  Multiplexer #(.select(2), .width(8), .enable("false")) multiplexer_1 (
    .in0(PC_4), .in1(adder_1_out), .in2(adder_1_out), .in3(Combined_end_of_splitter), .out(MUX_output),
    .sel(priority_encoder_1_out));
endmodule
