// Logisim project pipelining.circ as structural Verilog: 9 circuits, main circuit main
module main (
  input  Clear,
  output [7:0] PC,
  output [7:0] Zero,
  output [7:0] t0,
  output [7:0] t1,
  output [7:0] t2,
  output [7:0] t3,
  output [7:0] t4,
  output [7:0] t5,
  output [7:0] sp
);

  wire alu_8_by_art_1_p4, Clk_out, controll_1_alusrc, controll_1_beq, controll_1_bneq, controll_1_jump,
       controll_1_memread, controll_1_memtoreg, controll_1_memwrite, controll_1_regdst, controll_1_regwrite,
       controll_1_shift, ex_mem_reg_1_beq_2, ex_mem_reg_1_bneq_2, ex_mem_reg_1_memread_2,
       ex_mem_reg_1_memtoreg_2, ex_mem_reg_1_memwrite_2, ex_mem_reg_1_reg_wrt, ex_mem_reg_1_zero_2,
       hazard_detection_1_hazard, id_ex_reg_1_alusrc_2, id_ex_reg_1_beq_2, id_ex_reg_1_bneq_2,
       id_ex_reg_1_jump_2, id_ex_reg_1_memread_2, id_ex_reg_1_memtoreg_2, id_ex_reg_1_memwrite_2,
       id_ex_reg_1_reg_dst, id_ex_reg_1_reg_wrt_2, mem_wb_reg_1_memto_reg_2, mem_wb_reg_1_reg_write_2,
       multiplexer_7_out, not_1_out;
  wire [1:0] forward_unit_1_forwarb, forward_unit_1_forwarda;
  wire [2:0] controll_1_aluop, id_ex_reg_1_aluop;
  wire [3:0] ex_mem_reg_1_reg_rd_addrs_2, id_ex_reg_1_reg_rd_address_2, id_ex_reg_1_reg_rs_address_2,
       id_ex_reg_1_reg_rt_address_2, mem_wb_reg_1_reg_rd_address_2, multiplexer_5_out;
  wire [7:0] adder_1_out, adder_2_out, alu_8_by_art_1_p5, ex_mem_reg_1_alu_reslt, ex_mem_reg_1_pc_4_2,
       ex_mem_reg_1_reg_data_2_2, id_ex_reg_1_imm_2, id_ex_reg_1_pc_4_2, id_ex_reg_1_reg_rs_data,
       id_ex_reg_1_reg_rt_data, if_id_reg_1_pc_4_2, mem_wb_reg_1_alu_result_2, mem_wb_reg_1_read_data_2,
       multiplexer_1_out, multiplexer_2_out, multiplexer_3_out, multiplexer_4_out, multiplexer_6_out,
       multiplexer_8_out, ram_1_data, register_2_read_data_1, register_2_read_data_2;
  wire [19:0] if_id_reg_1_instruction_0_19_2, rom_1_data;

  not not_1 (not_1_out, hazard_detection_1_hazard);
  Clock Clk (.out(Clk_out));
  Register register_1 (.D(multiplexer_1_out), .en(not_1_out), .Q(PC), .clk(Clk_out), .clr(Clear));
  Multiplexer #(.width(8), .enable("false")) multiplexer_1 (
    .in0(multiplexer_2_out), .in1(if_id_reg_1_instruction_0_19_2[15:8]), .out(multiplexer_1_out),
    .sel(controll_1_jump));
  Multiplexer #(.width(8), .enable("false")) multiplexer_2 (
    .in0(adder_1_out), .in1(ex_mem_reg_1_pc_4_2), .out(multiplexer_2_out), .sel(multiplexer_7_out));
  Adder adder_1 (.a(PC), .b(8'h1), .out(adder_1_out));  // open: cin, cout
  ROM #(.dataWidth(20)) rom_1 (.addr(PC), .data(rom_1_data));  // open: sel
  If_Id_reg if_id_reg_1 (
    .Pc_4(adder_1_out), .Instruction_0_19(rom_1_data), .Stall(hazard_detection_1_hazard), .CLK(Clk_out),
    .CLR(Clear), .PC_4_2(if_id_reg_1_pc_4_2), .Instruction_0_19_2(if_id_reg_1_instruction_0_19_2));
  hazard_detection hazard_detection_1 (
    .ID_EX_MemRead(id_ex_reg_1_memread_2), .ID_EX_RegisterRt(id_ex_reg_1_reg_rt_address_2),
    .IF_ID_RegisterRs(if_id_reg_1_instruction_0_19_2[15:12]),
    .IF_ID_RegisterRt(if_id_reg_1_instruction_0_19_2[11:8]), .Hazard(hazard_detection_1_hazard));
  controll controll_1 (
    .in_1(if_id_reg_1_instruction_0_19_2[19:16]), .load_use(hazard_detection_1_hazard),
    .ALUOp(controll_1_aluop), .ALUSrc(controll_1_alusrc), .Bneq(controll_1_bneq), .Beq(controll_1_beq),
    .MemToReg(controll_1_memtoreg), .MemWrite(controll_1_memwrite), .MemRead(controll_1_memread),
    .RegWrite(controll_1_regwrite), .RegDst(controll_1_regdst), .Shift(controll_1_shift),
    .Jump(controll_1_jump));
  register register_2 (
    .Read_Register_1(if_id_reg_1_instruction_0_19_2[15:12]),
    .Read_Register_2(if_id_reg_1_instruction_0_19_2[11:8]), .Write_Register(mem_wb_reg_1_reg_rd_address_2),
    .Write_Data(multiplexer_8_out), .Write_Signal(mem_wb_reg_1_reg_write_2), .CLK(Clk_out), .Clear(Clear),
    .zero(Zero), .t0(t0), .t1(t1), .t2(t2), .t3(t3), .t4(t4), .t5(t5), .sp(sp),
    .Read_Data_1(register_2_read_data_1), .Read_Data_2(register_2_read_data_2));
  Id_Ex_reg id_ex_reg_1 (
    .CLR(Clear), .CLK(Clk_out), .pc_4(if_id_reg_1_pc_4_2), .reg_data_1(register_2_read_data_1),
    .reg_data_2(register_2_read_data_2), .IMM(if_id_reg_1_instruction_0_19_2[7:0]),
    .reg_rd_address(if_id_reg_1_instruction_0_19_2[7:4]),
    .reg_rs_address(if_id_reg_1_instruction_0_19_2[15:12]),
    .reg_rt_address(if_id_reg_1_instruction_0_19_2[11:8]), .Alu_op(controll_1_aluop),
    .reg_wrt(controll_1_regwrite), .MemtoReg(controll_1_memtoreg), .Memread(controll_1_memread),
    .Memwrite(controll_1_memwrite), .regdst(controll_1_regdst), .shift(controll_1_shift),
    .Jump(controll_1_jump), .AluSRC(controll_1_alusrc), .beq(controll_1_beq), .bneq(controll_1_bneq),
    .Pc_4_2(id_ex_reg_1_pc_4_2), .reg_rs_data(id_ex_reg_1_reg_rs_data),
    .reg_rt_data(id_ex_reg_1_reg_rt_data), .IMM_2(id_ex_reg_1_imm_2),
    .reg_rd_address_2(id_ex_reg_1_reg_rd_address_2), .reg_rs_address_2(id_ex_reg_1_reg_rs_address_2),
    .reg_rt_address_2(id_ex_reg_1_reg_rt_address_2), .Aluop(id_ex_reg_1_aluop),
    .reg_wrt_2(id_ex_reg_1_reg_wrt_2), .MemtoReg_2(id_ex_reg_1_memtoreg_2),
    .Memread_2(id_ex_reg_1_memread_2), .memwrite_2(id_ex_reg_1_memwrite_2), .reg_dst(id_ex_reg_1_reg_dst),
    .jump_2(id_ex_reg_1_jump_2), .Alusrc_2(id_ex_reg_1_alusrc_2), .beq_2(id_ex_reg_1_beq_2),
    .bneq_2(id_ex_reg_1_bneq_2));  // open: shift_2
  Multiplexer #(.select(2), .width(8), .enable("false")) multiplexer_3 (
    .in0(id_ex_reg_1_reg_rs_data), .in1(multiplexer_8_out), .in2(ex_mem_reg_1_alu_reslt),
    .out(multiplexer_3_out), .sel(forward_unit_1_forwarda));  // open: in3
  Multiplexer #(.select(2), .width(8), .enable("false")) multiplexer_4 (
    .in0(id_ex_reg_1_reg_rt_data), .in1(multiplexer_8_out), .in2(ex_mem_reg_1_alu_reslt),
    .out(multiplexer_4_out), .sel(forward_unit_1_forwarb));  // open: in3
  Multiplexer #(.width(4), .enable("false")) multiplexer_5 (
    .in0(id_ex_reg_1_reg_rt_address_2), .in1(id_ex_reg_1_reg_rd_address_2), .out(multiplexer_5_out),
    .sel(id_ex_reg_1_reg_dst));
  forward_unit forward_unit_1 (
    .EX_MEM_RegWrite(ex_mem_reg_1_reg_wrt), .EX_MEM_RegisterRD(ex_mem_reg_1_reg_rd_addrs_2),
    .ID_EX_RegisterRs(id_ex_reg_1_reg_rs_address_2), .ID_EX_RegisterRt(id_ex_reg_1_reg_rt_address_2),
    .Mem_WB_RegisterRd(mem_wb_reg_1_reg_rd_address_2), .MEM_WB_RegWrite(mem_wb_reg_1_reg_write_2),
    .ForwardA(forward_unit_1_forwarda), .ForwarB(forward_unit_1_forwarb));
  Multiplexer #(.width(8), .enable("false")) multiplexer_6 (
    .in0(multiplexer_4_out), .in1(id_ex_reg_1_imm_2), .out(multiplexer_6_out), .sel(id_ex_reg_1_alusrc_2));
  Adder adder_2 (.a(id_ex_reg_1_pc_4_2), .b(id_ex_reg_1_imm_2), .out(adder_2_out));  // open: cin, cout
  // ALU_8_by_ART alu_8_by_art_1: pin names not known; wires that end beside it: multiplexer_3_out, multiplexer_6_out, id_ex_reg_1_aluop, alu_8_by_art_1_p4, alu_8_by_art_1_p5
  EX_Mem_reg ex_mem_reg_1 (
    .pc_4(adder_2_out), .alu_result(alu_8_by_art_1_p5), .reg_data_2(multiplexer_4_out),
    .reg_rd_addrs(multiplexer_5_out), .regwrt(id_ex_reg_1_reg_wrt_2), .MemtoReg(id_ex_reg_1_memtoreg_2),
    .Jump(id_ex_reg_1_jump_2), .Memread(id_ex_reg_1_memread_2), .Memwrite(id_ex_reg_1_memwrite_2),
    .beq(id_ex_reg_1_beq_2), .bneq(id_ex_reg_1_bneq_2), .Zero(alu_8_by_art_1_p4), .CLR(Clear), .clk(Clk_out),
    .pc_4_2(ex_mem_reg_1_pc_4_2), .alu_reslt(ex_mem_reg_1_alu_reslt),
    .reg_data_2_2(ex_mem_reg_1_reg_data_2_2), .reg_rd_addrs_2(ex_mem_reg_1_reg_rd_addrs_2),
    .reg_wrt(ex_mem_reg_1_reg_wrt), .MemtoReg_2(ex_mem_reg_1_memtoreg_2), .Memread_2(ex_mem_reg_1_memread_2),
    .memwrite_2(ex_mem_reg_1_memwrite_2), .beq_2(ex_mem_reg_1_beq_2), .bneq_2(ex_mem_reg_1_bneq_2),
    .zero_2(ex_mem_reg_1_zero_2));  // open: Jump_2
  Multiplexer #(.enable("false")) multiplexer_7 (
    .in0(ex_mem_reg_1_beq_2), .in1(ex_mem_reg_1_bneq_2), .out(multiplexer_7_out), .sel(ex_mem_reg_1_zero_2));
  RAM #(.bus("separate")) ram_1 (
    .addr(ex_mem_reg_1_alu_reslt), .din(ex_mem_reg_1_reg_data_2_2), .data(ram_1_data),
    .str(ex_mem_reg_1_memwrite_2), .sel(1'b1), .clk(Clk_out), .ld(ex_mem_reg_1_memread_2), .clr(Clear));
  Mem_wb_reg mem_wb_reg_1 (
    .Reg_Write(ex_mem_reg_1_reg_wrt), .Memto_Reg(ex_mem_reg_1_memtoreg_2), .Read_data(ram_1_data),
    .Alu_result(ex_mem_reg_1_alu_reslt), .Reg_rd_address(ex_mem_reg_1_reg_rd_addrs_2), .clock(Clk_out),
    .Clear(Clear), .Reg_write_2(mem_wb_reg_1_reg_write_2), .Memto_reg_2(mem_wb_reg_1_memto_reg_2),
    .Read_Data_2(mem_wb_reg_1_read_data_2), .Alu_Result_2(mem_wb_reg_1_alu_result_2),
    .Reg_Rd_address_2(mem_wb_reg_1_reg_rd_address_2));
  Multiplexer #(.width(8), .enable("false")) multiplexer_8 (
    .in0(mem_wb_reg_1_alu_result_2), .in1(mem_wb_reg_1_read_data_2), .out(multiplexer_8_out),
    .sel(mem_wb_reg_1_memto_reg_2));

  // Notes on the sheet:
  //   contents of rom_1 (hex, n*v repeats v):
  //   107ff 10205 1040a 24250 10414 f4560
  //   Alu_op
  //   Alu_src
  //   Bneq
  //   Beq
  //   MemToReg
  //   MemWrite
  //   MemRead
  //   RegWrite
  //   RegDst
  //   Shift
  //   Jump
  //   Reg_Data_1
  //   Reg_Data_2
  //   Branch_Pc_source
endmodule

module register (
  input  [3:0] Read_Register_1,
  input  [3:0] Read_Register_2,
  input  [3:0] Write_Register,
  input  [7:0] Write_Data,
  input  Write_Signal,
  input  CLK,
  input  Clear,
  output [7:0] Read_Data_1,
  output [7:0] Read_Data_2,
  output [7:0] sp,
  output [7:0] zero,
  output [7:0] t5,
  output [7:0] t0,
  output [7:0] t4,
  output [7:0] t1,
  output [7:0] t2,
  output [7:0] t3
);

  wire and_1_out, and_2_out, and_3_out, and_4_out, and_5_out, and_6_out, and_7_out, and_8_out,
       decoder_1_out0, decoder_1_out1, decoder_1_out2, decoder_1_out3, decoder_1_out4, decoder_1_out5,
       decoder_1_out6, decoder_1_out7, multiplexer_1_out, multiplexer_3_out;
  wire [7:0] multiplexer_2_out;

  Decoder #(.select(4), .enable("false")) decoder_1 (
    .out0(decoder_1_out0), .out1(decoder_1_out1), .out2(decoder_1_out2), .out3(decoder_1_out3),
    .out4(decoder_1_out4), .out5(decoder_1_out5), .out6(decoder_1_out6), .out7(decoder_1_out7),
    .sel(Write_Register));  // open: out8, out9, out10, out11, out12, out13, out14, out15
  and and_1 (and_1_out, decoder_1_out0, 1'b0);
  and and_2 (and_2_out, decoder_1_out1, Write_Signal);
  and and_3 (and_3_out, decoder_1_out2, Write_Signal);
  and and_4 (and_4_out, decoder_1_out3, Write_Signal);
  and and_5 (and_5_out, decoder_1_out4, Write_Signal);
  and and_6 (and_6_out, decoder_1_out5, Write_Signal);
  and and_7 (and_7_out, decoder_1_out6, Write_Signal);
  and and_8 (and_8_out, decoder_1_out7, Write_Signal);
  Multiplexer #(.enable("false")) multiplexer_1 (.in0(and_8_out), .in1(Clear), .out(multiplexer_1_out), .sel(Clear));
  Multiplexer #(.width(8), .enable("false")) multiplexer_2 (
    .in0(Write_Data), .in1({8{1'b1}}), .out(multiplexer_2_out), .sel(Clear));
  Register u_zero (.D(Write_Data), .en(and_1_out), .Q(zero), .clk(CLK), .clr(Clear));
  Register u_t0 (.D(Write_Data), .en(and_2_out), .Q(t0), .clk(CLK), .clr(Clear));
  Register u_t1 (.D(Write_Data), .en(and_3_out), .Q(t1), .clk(CLK), .clr(Clear));
  Register u_t2 (.D(Write_Data), .en(and_4_out), .Q(t2), .clk(CLK), .clr(Clear));
  Register u_t3 (.D(Write_Data), .en(and_5_out), .Q(t3), .clk(CLK), .clr(Clear));
  Register u_t4 (.D(Write_Data), .en(and_6_out), .Q(t4), .clk(CLK), .clr(Clear));
  Register u_t5 (.D(Write_Data), .en(and_7_out), .Q(t5), .clk(CLK), .clr(Clear));
  Register u_sp (.D(multiplexer_2_out), .en(multiplexer_1_out), .Q(sp), .clk(multiplexer_3_out));  // open: clr
  Multiplexer #(.enable("false")) multiplexer_3 (.in0(CLK), .in1(Clear), .out(multiplexer_3_out), .sel(Clear));
  Multiplexer #(.select(4), .width(8), .enable("false")) multiplexer_4 (
    .in0(zero), .in1(t0), .in2(t1), .in3(t2), .in4(t3), .in5(t4), .in6(t5), .in7(sp), .out(Read_Data_1),
    .sel(Read_Register_1));  // open: in8, in9, in10, in11, in12, in13, in14, in15
  Multiplexer #(.select(4), .width(8), .enable("false")) multiplexer_5 (
    .in0(zero), .in1(t0), .in2(t1), .in3(t2), .in4(t3), .in5(t4), .in6(t5), .in7(sp), .out(Read_Data_2),
    .sel(Read_Register_2));  // open: in8, in9, in10, in11, in12, in13, in14, in15
endmodule

module controll (
  input  [3:0] in_1,
  input  load_use,
  output [2:0] ALUOp,
  output ALUSrc,
  output Bneq,
  output Beq,
  output MemToReg,
  output MemWrite,
  output MemRead,
  output RegWrite,
  output RegDst,
  output Shift,
  output Jump
);

  wire [12:0] rom_1_data;

  ROM #(.addrWidth(4), .dataWidth(13)) rom_1 (.addr(in_1), .data(rom_1_data));  // open: sel
  Multiplexer #(.width(13), .enable("false")) multiplexer_1 (
    .in0(rom_1_data), .in1({13{1'b0}}),
    .out({Jump, Shift, RegDst, RegWrite, MemRead, MemWrite, MemToReg, Beq, Bneq, ALUSrc, ALUOp}),
    .sel(load_use));

  // Notes on the sheet:
  //   contents of rom_1 (hex, n*v repeats v):
  //   603 208 601 209 1000 11 88 348 602 e0e e0d 20b 604 20a 21 600
endmodule

// IF/ID_reg
module If_Id_reg (
  input  [7:0] Pc_4,
  input  [19:0] Instruction_0_19,
  input  Stall,
  input  CLK,
  input  CLR,
  output [7:0] PC_4_2,
  output [19:0] Instruction_0_19_2
);

  wire not_1_out;

  not not_1 (not_1_out, Stall);
  Register u_PC_4 (.D(Pc_4), .en(not_1_out), .Q(PC_4_2), .clk(CLK), .clr(CLR));
  Register #(.width(20)) IF_ID (.D(Instruction_0_19), .en(not_1_out), .Q(Instruction_0_19_2), .clk(CLK), .clr(CLR));
endmodule

// ID/EX_reg
module Id_Ex_reg (
  input  CLR,
  input  CLK,
  input  [7:0] pc_4,
  input  [7:0] reg_data_1,
  input  [7:0] reg_data_2,
  input  [7:0] IMM,
  input  [3:0] reg_rd_address,
  input  [3:0] reg_rs_address,
  input  [3:0] reg_rt_address,
  input  [2:0] Alu_op,
  input  reg_wrt,
  input  MemtoReg,
  input  Memread,
  input  Memwrite,
  input  regdst,
  input  shift,
  input  Jump,
  input  AluSRC,
  input  beq,
  input  bneq,
  output [7:0] Pc_4_2,
  output [7:0] reg_rs_data,
  output [7:0] reg_rt_data,
  output [7:0] IMM_2,
  output [3:0] reg_rd_address_2,
  output [3:0] reg_rs_address_2,
  output [3:0] reg_rt_address_2,
  output [2:0] Aluop,
  output reg_wrt_2,
  output MemtoReg_2,
  output Memread_2,
  output memwrite_2,
  output reg_dst,
  output shift_2,
  output jump_2,
  output Alusrc_2,
  output beq_2,
  output bneq_2
);

  Register read_reg1_data (.D(pc_4), .en(1'b1), .Q(Pc_4_2), .clk(CLK), .clr(CLR));
  Register read_reg1_data_2 (.D(reg_data_1), .en(1'b1), .Q(reg_rs_data), .clk(CLK), .clr(CLR));
  Register read_reg2_data (.D(reg_data_2), .en(1'b1), .Q(reg_rt_data), .clk(CLK), .clr(CLR));
  Register u_Imm (.D(IMM), .en(1'b1), .Q(IMM_2), .clk(CLK), .clr(CLR));
  Register #(.width(4)) reg_rd (.D(reg_rd_address), .en(1'b1), .Q(reg_rd_address_2), .clk(CLK), .clr(CLR));
  Register #(.width(4)) reg_rs (.D(reg_rs_address), .en(1'b1), .Q(reg_rs_address_2), .clk(CLK), .clr(CLR));
  Register #(.width(4)) reg_rt (.D(reg_rt_address), .en(1'b1), .Q(reg_rt_address_2), .clk(CLK), .clr(CLR));
  Register #(.width(3)) register_1 (.D(Alu_op), .en(1'b1), .Q(Aluop), .clk(CLK), .clr(CLR));
  Register #(.width(1)) register_2 (.D(reg_wrt), .en(1'b1), .Q(reg_wrt_2), .clk(CLK), .clr(CLR));
  Register #(.width(1)) register_3 (.D(MemtoReg), .en(1'b1), .Q(MemtoReg_2), .clk(CLK));  // open: clr
  Register #(.width(1)) register_4 (.D(Memread), .en(1'b1), .Q(Memread_2), .clk(CLK), .clr(CLR));
  Register #(.width(1)) register_5 (.D(Memwrite), .en(1'b1), .Q(memwrite_2), .clk(CLK), .clr(CLR));
  Register #(.width(1)) register_6 (.D(regdst), .en(1'b1), .Q(reg_dst), .clk(CLK), .clr(CLR));
  Register #(.width(1)) register_7 (.D(shift), .en(1'b1), .Q(shift_2), .clk(CLK), .clr(CLR));
  Register #(.width(1)) register_8 (.D(Jump), .en(1'b1), .Q(jump_2), .clk(CLK), .clr(CLR));
  Register #(.width(1)) register_9 (.D(AluSRC), .en(1'b1), .Q(Alusrc_2), .clk(CLK), .clr(CLR));
  Register #(.width(1)) register_10 (.D(beq), .en(1'b1), .Q(beq_2), .clk(CLK), .clr(CLR));
  Register #(.width(1)) register_11 (.D(bneq), .en(1'b1), .Q(bneq_2), .clk(CLK), .clr(CLR));
endmodule

// Ex/Mem_reg
module EX_Mem_reg (
  input  clk,
  input  CLR,
  input  [7:0] pc_4,
  input  [7:0] alu_result,
  input  [7:0] reg_data_2,
  input  [3:0] reg_rd_addrs,
  input  regwrt,
  input  MemtoReg,
  input  Jump,
  input  Memread,
  input  Memwrite,
  input  beq,
  input  bneq,
  input  Zero,
  output [7:0] pc_4_2,
  output [7:0] alu_reslt,
  output [7:0] reg_data_2_2,
  output [3:0] reg_rd_addrs_2,
  output reg_wrt,
  output MemtoReg_2,
  output Jump_2,
  output Memread_2,
  output memwrite_2,
  output beq_2,
  output bneq_2,
  output zero_2
);

  Register u_alu_result (.D(pc_4), .en(1'b1), .Q(pc_4_2), .clk(clk), .clr(CLR));
  Register alu_result_2 (.D(alu_result), .en(1'b1), .Q(alu_reslt), .clk(clk), .clr(CLR));
  Register reg_data2 (.D(reg_data_2), .en(1'b1), .Q(reg_data_2_2), .clk(CLR), .clr(CLR));
  Register #(.width(4)) reg_rd (.D(reg_rd_addrs), .en(1'b1), .Q(reg_rd_addrs_2), .clk(clk), .clr(CLR));
  Register #(.width(1)) register_1 (.D(regwrt), .en(1'b1), .Q(reg_wrt), .clk(clk), .clr(CLR));
  Register #(.width(1)) register_2 (.D(MemtoReg), .en(1'b1), .Q(MemtoReg_2), .clk(clk), .clr(CLR));
  Register #(.width(1)) register_3 (.D(Jump), .en(1'b1), .Q(Jump_2), .clk(clk), .clr(CLR));
  Register #(.width(1)) register_4 (.D(Memread), .en(1'b1), .Q(Memread_2), .clk(clk), .clr(CLR));
  Register #(.width(1)) register_5 (.D(Memwrite), .en(1'b1), .Q(memwrite_2), .clk(clk), .clr(CLR));
  Register #(.width(1)) register_6 (.D(beq), .en(1'b1), .Q(beq_2), .clk(clk), .clr(CLR));
  Register #(.width(1)) register_7 (.D(bneq), .en(1'b1), .Q(bneq_2), .clk(clk), .clr(CLR));
  Register #(.width(1)) register_8 (.D(Zero), .en(1'b1), .Q(zero_2), .clk(clk), .clr(CLR));

  // Notes on the sheet:
  //   Reg_Data_1
endmodule

// Forward_unit
module forward_unit (
  input  EX_MEM_RegWrite,
  input  [3:0] EX_MEM_RegisterRD,
  input  [3:0] ID_EX_RegisterRs,
  input  [3:0] ID_EX_RegisterRt,
  input  [3:0] Mem_WB_RegisterRd,
  input  MEM_WB_RegWrite,
  output [1:0] ForwardA,
  output [1:0] ForwarB
);

  wire comparator_1_eq, comparator_2_eq, comparator_3_eq, comparator_4_eq, comparator_5_eq, comparator_6_eq;
  wire [3:0] and_4_out;

  Comparator #(.width(4), .mode("unsigned")) comparator_1 (
    .a(EX_MEM_RegisterRD), .b(4'b0000), .eq(comparator_1_eq));  // open: gt, lt
  Comparator #(.width(4), .mode("unsigned")) comparator_2 (
    .a(EX_MEM_RegisterRD), .b(ID_EX_RegisterRs), .eq(comparator_2_eq));  // open: gt, lt
  Comparator #(.width(4), .mode("unsigned")) comparator_3 (
    .a(Mem_WB_RegisterRd), .b(ID_EX_RegisterRs), .eq(comparator_3_eq));  // open: gt, lt
  Comparator #(.width(4), .mode("unsigned")) comparator_4 (
    .a(EX_MEM_RegisterRD), .b(ID_EX_RegisterRt), .eq(comparator_4_eq));  // open: gt, lt
  Comparator #(.width(4), .mode("unsigned")) comparator_5 (
    .a(Mem_WB_RegisterRd), .b(ID_EX_RegisterRt), .eq(comparator_5_eq));  // open: gt, lt
  Comparator #(.width(4), .mode("unsigned")) comparator_6 (
    .a(Mem_WB_RegisterRd), .b(4'b0000), .eq(comparator_6_eq));  // open: gt, lt
  and and_1 (and_4_out[3], ~comparator_1_eq, EX_MEM_RegWrite, comparator_2_eq);  // AND_Gate
  and and_2 (and_4_out[1], MEM_WB_RegWrite, ~comparator_6_eq, comparator_3_eq);  // AND_Gate
  and and_3 (and_4_out[2], EX_MEM_RegWrite, ~comparator_1_eq, comparator_4_eq);  // AND_Gate
  and and_4 (and_4_out[0], comparator_5_eq, ~comparator_6_eq, MEM_WB_RegWrite);  // AND_Gate
  ROM #(.addrWidth(4), .dataWidth(4)) rom_1 (.addr(and_4_out), .data({ForwardA, ForwarB}), .sel(1'b1));

  // Notes on the sheet:
  //   contents of rom_1 (hex, n*v repeats v):
  //   0 1 4 5 2 2 6 6 8 9 8 9 4*a
endmodule

module Mem_wb_reg (
  input  Reg_Write,
  input  Memto_Reg,
  input  [7:0] Read_data,
  input  [7:0] Alu_result,
  input  [3:0] Reg_rd_address,
  input  clock,
  input  Clear,
  output Reg_write_2,
  output Memto_reg_2,
  output [7:0] Read_Data_2,
  output [7:0] Alu_Result_2,
  output [3:0] Reg_Rd_address_2
);

  Register #(.width(1)) register_1 (.D(Reg_Write), .en(1'b1), .Q(Reg_write_2), .clk(clock), .clr(Clear));
  Register #(.width(1)) register_2 (.D(Memto_Reg), .en(1'b1), .Q(Memto_reg_2), .clk(clock), .clr(Clear));
  Register u_alu_result (.D(Read_data), .en(1'b1), .Q(Read_Data_2), .clk(clock), .clr(Clear));
  Register u_alu_result_2 (.D(Alu_result), .en(1'b1), .Q(Alu_Result_2), .clk(clock), .clr(Clear));
  Register #(.width(4)) reg_rd (.D(Reg_rd_address), .en(1'b1), .Q(Reg_Rd_address_2), .clk(clock), .clr(Clear));
endmodule

module hazard_detection (
  input  ID_EX_MemRead,
  input  [3:0] ID_EX_RegisterRt,
  input  [3:0] IF_ID_RegisterRs,
  input  [3:0] IF_ID_RegisterRt,
  output Hazard
);

  wire comparator_1_eq, comparator_2_eq, or_1_out;

  Comparator #(.width(4), .mode("unsigned")) comparator_1 (
    .a(ID_EX_RegisterRt), .b(IF_ID_RegisterRs), .eq(comparator_1_eq));  // open: gt, lt
  Comparator #(.width(4), .mode("unsigned")) comparator_2 (
    .a(ID_EX_RegisterRt), .b(IF_ID_RegisterRt), .eq(comparator_2_eq));  // open: gt, lt
  or or_1 (or_1_out, comparator_1_eq, comparator_2_eq);
  and and_1 (Hazard, ID_EX_MemRead, or_1_out);
endmodule
